# Fritzing sketch SeniorProjectFritz (saved by Fritzing 0.9.3b)
breadboards: 1

parts:
  Part1 = Arduino Mega 2560 (Rev3)
  LCD1 = LCD screen
  J1 = Basic Servo
  R1 = Rotary Potentiometer (Small) [maximum_resistance=100kΩ package=THT]
  KEYPAD1 = Membrane Matrix Keypad
  LED1 = RGB LED (com. anode, rbg) [package="5 mm [THT]"]
  J2 = Piezo Speaker
  JL012-13-5_1 = JL012-13-5.2 Lever (Limit) Switch SPDT + NO + NC [part_number=JL012-13-5.2]
  R2 = Resistor [tolerance=±5% resistance=220 package="2010 [SMD]"]
  R3 = Resistor [tolerance=±5% resistance=220 package="2010 [SMD]"]

nets:
  N1: Part1.D13_PWM, LCD1.DB7
  N2: Part1.D12_PWM, LCD1.DB6
  N3: Part1.D11_PWM, LCD1.DB5
  N4: Part1.D10_PWM, LCD1.DB4
  N5: Part1.D9_PWM, LCD1.E
  N6: Part1.D8_PWM, LCD1.RS
  5V: Part1.5V, LCD1.VDD, LCD1.LED+, J1.vcc, R1.leg1
  GND: Part1.GND, LCD1.VSS, LCD1.R/W, LCD1.LED-, J1.gnd, R1.leg2, LED1.common_anode, J2.pin1, JL012-13-5_1.NC
  N7: Part1.D2_PWM, J2.pin2
  N8: Part1.D3_PWM, J1.pulse
  N9: Part1.D5_PWM, Part1.D6_PWM, R2.Pin_1, R3.Pin_1
  N10: Part1.D7_PWM, JL012-13-5_1.C
  N11: Part1.D39, KEYPAD1.5
  N12: Part1.D41, KEYPAD1.6
  N13: Part1.D43, KEYPAD1.7
  N14: Part1.D45, KEYPAD1.1
  N15: Part1.D47, KEYPAD1.2
  N16: Part1.D49, KEYPAD1.3
  N17: Part1.D51, KEYPAD1.4
  N18: LCD1.V0, R1.wiper
  N19: LED1.red_cathode, R2.Pin_0
  N20: LED1.green_cathode, R3.Pin_0

custom parts:
  Membrane Matrix Keypad: Membrane Matrix 3x4 Keypad
  JL012-13-5.2 Lever (Limit) Switch SPDT + NO + NC: Micro Switch; Model No.: JL012-13.5-2; Actuator Action: Momentary; Actuator Type: Hinge Lever; Contact Configuration: 1NO, 1NC (SPDT) Temperature -25~65℃；Relative humidity: below 85%; Rate Voltage: 125V AC; Rated Current: 1A.

// code stored in the sketch: SeniorProjectCode.ino
//Limit Switch
#define LIMIT_SWITCH_PIN 0


//Keypad
#include <Keypad.h>
const byte ROWS = 4; 
const byte COLS = 3; 
char hexaKeys[ROWS][COLS] = {
  {'1', '2', '3'},
  {'4', '5', '6'},
  {'7', '8', '9'},
  {'*', '0', '#'}
};
byte rowPins[ROWS] = {45, 47, 49, 51}; 
byte colPins[COLS] = {39, 41, 43}; 
Keypad customKeypad = Keypad(makeKeymap(hexaKeys), rowPins, colPins, ROWS, COLS); 


//LCD
#include <LiquidCrystal.h>
const int rs = 13, en = 12, d4 = 11, d5 = 10, d6 = 9, d7 = 8;
LiquidCrystal lcd(rs, en, d4, d5, d6, d7);


//LED Red and Green
#define GREEN 6
#define RED 5

//Servo
#include <Servo.h>
Servo myservo;  // create servo object to control a servo


/*
//Potentiometer
#define potPin A3
int potVal = 0;
*/

//Limit Switch
int limitSwitch = 7;


//Buzzer
#define BUZZER 2

//Passcode
#define Password_Length 8 
char Data[Password_Length]; 
char Master[Password_Length] = "1234567"; 
byte data_count = 0, master_count = 0;
bool Pass_is_good;
char customKey;
bool Status = 1;

void setup() {
  // put your setup code here, to run once:
  pinMode(GREEN, OUTPUT);
  pinMode(RED, OUTPUT);
  digitalWrite(RED, LOW);
  digitalWrite(GREEN, HIGH);
  pinMode(BUZZER, OUTPUT);
  noTone(BUZZER);
  myservo.attach(3); 
  Serial.begin(9600); //For both limit switch and Keypad
  pinMode(LIMIT_SWITCH_PIN, INPUT);
  lcd.begin(16, 2);
  lcd.print("Monitoring...");
  pinMode(limitSwitch, INPUT_PULLUP);
 
}



void loop() {
  // put your main code here, to run repeatedly:
  /*
  myservo.write(0);
  delay(150);
  myservo.write(1023); 
  delay(150);
  */
  //potVal = analogRead(potPin);
  //Serial.println(potVal);
  if (digitalRead(limitSwitch) == 0){
    delay(1500);
    while (digitalRead(limitSwitch) == 0){
    lcd.print("Alert!");
    tone(BUZZER, 1000);
    digitalWrite(RED, HIGH);
    digitalWrite(GREEN, LOW);
    delay(200);
    lcd.clear();
    noTone(BUZZER);
    digitalWrite(RED, LOW);
    delay(200);
    digitalRead(limitSwitch);
    }
  }
  else {
    noTone(BUZZER);
    digitalWrite(RED, LOW);
    digitalWrite(GREEN, HIGH);
  }
  
  customKey = customKeypad.getKey();
  if (customKey){
    Data[data_count] = customKey; 
    lcd.setCursor(data_count,1); 
    lcd.print(Data[data_count]); 
    data_count++; 
    }

  if(data_count == Password_Length-1){
    lcd.clear();

    if(!strcmp(Data, Master)){
      lcd.print("Correct");
      delay(5000);
      if (Status == 1){
        myservo.write(1023);
        Status = 0;
        Serial.print(Status);
      }
      else if (Status == 0){
        myservo.write(0);
       Status = 1;
       Serial.print(Status);
      }
      }
    else{
      lcd.print("Incorrect");
      tone(BUZZER, 1000);
      delay(500);
      noTone(BUZZER);
      delay(500);
      }
    
    lcd.clear();
    lcd.print("Monitoring");
    clearData();  
  }
}

  /*
  if (digitalRead(LIMIT_SWITCH_PIN) == LOW) // should be high
  {
    Serial.println("Activated!");
  }
 
  else
  {
  }
  lcd.setCursor(0, 1);
  // Print a message to the LCD.
  lcd.print("hello, world!");
}
*/
void clearData(){
  while(data_count !=0){
    Data[data_count--] = 0; 
  }
  return;
}
