# Fritzing sketch Team1Circuit (saved by Fritzing 0.9.3b)
breadboards: 1

parts:
  Part1 = Adafruit Metro with Headers [part_number="Adafruit #2488"]
  KEYPAD1 = Membrane Matrix Keypad
  BAT1 = BC9VPC [package=bc9vpc]
  U1 = POT [package=pot_mammoth]
  R1 = Resistor [tolerance=±5% resistance=10k package="0805 [SMD]"]
  R2 = Resistor [tolerance=±5% resistance=220 package="2512 [SMD]"]
  G = Blue smd LED [package="0603 [SMD]"]
  R = Blue smd LED [package="0603 [SMD]"]
  R3 = Resistor [tolerance=±5% resistance=220 package="2512 [SMD]"]

nets:
  N1: Part1.AD3, U1.S
  N2: Part1.GND, U1.A, G.cathode, R.cathode
  N3: Part1.IO8, KEYPAD1.1
  N4: Part1.IO7, KEYPAD1.2
  N5: Part1.IO6, KEYPAD1.3
  N6: Part1.IO5, KEYPAD1.4
  N7: Part1.IO4, KEYPAD1.7
  N8: Part1.IO3, KEYPAD1.6
  N9: Part1.IO2, KEYPAD1.5
  N10: Part1.IO1, R3.Pin_0
  N11: Part1.IO0, R2.Pin_0
  N12: Part1.+5V, R1.Pin_1
  N13: Part1.VIN, BAT1.V+
  N14: U1.E, R1.Pin_0
  N15: R2.Pin_1, G.anode
  N16: R.anode, R3.Pin_1

custom parts:
  Adafruit Metro with Headers: We sure love the ATmega328 here at Adafruit, and we use them a lot for our own projects. The processor has plenty of GPIO, Analog inputs, hardware UART SPI and I2C, timers and PWM galore - just enough for most simple projects. When we need to go small, we use a Pro Trinket 3V or 5V, but when size isn't as much of a concern, and an USB-serial converter is required, we reach for an Adafruit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
  Membrane Matrix Keypad: Membrane Matrix 3x4 Keypad
  Blue smd LED: A generic blue LED (~1.8V)
