# Fritzing sketch Team1Circuitv2 (saved by Fritzing 0.9.3b)
breadboards: 1

parts:
  BAT1 = BC9VPC [package=bc9vpc]
  R2 = Resistor [tolerance=±5% resistance=220 package="2512 [SMD]"]
  G = Blue smd LED [package="0603 [SMD]"]
  R = Blue smd LED [package="0603 [SMD]"]
  R3 = Resistor [tolerance=±5% resistance=220 package="2512 [SMD]"]
  J1 = Basic Servo
  SP1 = SPEAKER [package=pcb_mount_speaker]
  Part2 = Adafruit Metro M0 Express
  S1 = D2F-FL Omron Snap Action Limit Switch with Level
  KEYPAD1 = Membrane Matrix Keypad
  U1 = LCD-16X2 [package=lcd-16x2]
  U2 = POT [package=pot_alpha_rv16af-20]

nets:
  N1: BAT1.V+, Part2.VIN
  N2: R2.Pin_0, Part2.D0
  N3: R2.Pin_1, G.anode
  GND: G.cathode, R.cathode, J1.gnd, SP1.-, Part2.GND, S1.Pin_1, U1.VSS, U1.R_W, U2.A
  N4: R.anode, R3.Pin_1
  N5: R3.Pin_0, Part2.D1
  VCC: J1.vcc, Part2.+5V, U1.VDD, U2.E
  N6: J1.pulse, Part2.D4
  N7: SP1.+, Part2.D13
  N8: Part2.A0, KEYPAD1.1
  N9: Part2.A1, KEYPAD1.2
  N10: Part2.A2, KEYPAD1.3
  N11: Part2.A3, KEYPAD1.4
  N12: Part2.A4, KEYPAD1.5
  N13: Part2.A5, KEYPAD1.6
  N14: Part2.D10, U1.RS
  N15: Part2.D9, U1.E
  N16: Part2.D8, U1.DB4
  N17: Part2.D7, U1.DB5
  N18: Part2.D6, U1.DB6
  N19: Part2.D5, U1.DB7
  N20: Part2.D3, S1.Pin_3
  N21: Part2.D2, KEYPAD1.7
  N22: U1.VO, U2.S

custom parts:
  Blue smd LED: A generic blue LED (~1.8V)
  Adafruit Metro M0 Express: Metro is our series of microcontroller boards for use with the Arduino IDE. This new Metro board looks a whole lot like our original Metro 328, but with a huge upgrade. Instead of the ATmega328, this Metro features a ATSAMD21G18 chip, an ARM Cortex M0+. It's our first Metro that is designed for use with CircuitPython! CircuitPython is our beginner-oriented flavor of MicroPython - and as the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
  D2F-FL Omron Snap Action Limit Switch with Level: Snap action switch with stainless steel lever.
  Membrane Matrix Keypad: Membrane Matrix 3x4 Keypad
